// Logisim project simulation.circ as structural Verilog: 1 circuit, main circuit main
module main (
  input  A0,
  input  B0,
  input  A1,
  input  B1,
  output S0,
  output S1,
  output C
);

  wire and_1_out, and_2_out, and_3_out, xor_2_out;

  xor xor_1 (S0, A0, B0);
  and and_1 (and_1_out, A0, B0);
  xor xor_2 (xor_2_out, A1, B1);
  and and_2 (and_2_out, A1, B1);
  xor xor_3 (S1, xor_2_out, and_1_out);
  and and_3 (and_3_out, xor_2_out, and_1_out);
  or or_1 (C, and_3_out, and_2_out);
endmodule
